# Fritzing sketch raspberry (saved by Fritzing 0.9.2b)
breadboards: 1

parts:
  Raspberry_Pi1 = Raspberry Pi B+
  Eleman1 = Analog Digital MUX Breakout

nets:
  N1: Raspberry_Pi1.GPIO25, Eleman1.S3
  N2: Raspberry_Pi1.GPIO24, Eleman1.S2
  N3: Raspberry_Pi1.GPIO23, Eleman1.S1
  N4: Raspberry_Pi1.GPIO18, Eleman1.S0
  GND: Raspberry_Pi1.GND, Eleman1.GND, Eleman1.EN
  5V: Raspberry_Pi1.5V, Eleman1.VCC
